# Fritzing sketch LivingRoomLamp (saved by Fritzing 0.8.5b)
circuit board: 5.2cm x 3.2cm
breadboards: 1

parts:
  4 = female pin header, 3 pins [form="♀ (female)"]
  7 = female pin header, 3 pins [form="♀ (female)"]
  8 = female pin header, 3 pins [form="♀ (female)"]
  12V = female pin header, 2 pins [form="♀ (female)"]
  TB = MOSFET-NCHANNEL [package=to220v]
  TG = MOSFET-NCHANNEL [package=to220v]
  TR = MOSFET-NCHANNEL [package=to220v]
  B_R_G_+ = female pin header, 4 pins [form="♀ (female)"]
  HC-05 = female pin header, 6 pins [form="♀ (female)"]
  IR1 = TSOP312.., 314.. [package=THT]
  MAGN_RESET = Reed switch [package=THT]
  10 = female pin header, 3 pins [form="♀ (female)"]
  proxim = female pin header, 2 pins [form="♀ (female)"]
  proxy1 = female pin header, 1 pin [form="♀ (female)"]
  J1 = female pin header, 1 pin [form="♀ (female)"]
  Arduino_Pro_Mini_5V = Arduino Pro Mini v13
  GND = female pin header, 1 pin [form="♀ (female)"]
  VCC = female pin header, 1 pin [form="♀ (female)"]
  GND1 = female pin header, 1 pin [form="♀ (female)"]  # not connected
  nc = female pin header, 2 pins [form="♀ (female)"]  # not connected

nets:
  N1: 4.pin1, 7.pin1, 8.pin1, HC-05.pin2, IR1.Vs, 10.pin1, Arduino_Pro_Mini_5V.VCC, VCC.pin1
  N2: 4.pin2, Arduino_Pro_Mini_5V.D4
  GND: 4.pin3, 7.pin3, 8.pin3, 12V.pin2, TB.S, TG.S, TR.S, HC-05.pin3, IR1.GND, MAGN_RESET.pin_2, 10.pin3, J1.pin1, Arduino_Pro_Mini_5V.GND, GND.pin1
  N3: 7.pin2, Arduino_Pro_Mini_5V.D7
  N4: 8.pin2, Arduino_Pro_Mini_5V.D8
  12V: 12V.pin1, B_R_G_+.pin1, Arduino_Pro_Mini_5V.RAW
  N5: TB.G, Arduino_Pro_Mini_5V.D5_PWM
  N6: TB.D, B_R_G_+.pin4
  N7: TG.G, Arduino_Pro_Mini_5V.D6_PWM
  N8: TG.D, B_R_G_+.pin2
  N9: TR.G, Arduino_Pro_Mini_5V.D9_PWM
  N10: TR.D, B_R_G_+.pin3
  N11: HC-05.pin1, Arduino_Pro_Mini_5V.D11_PWM/MOSI
  N12: HC-05.pin4, Arduino_Pro_Mini_5V.D1/RX
  N13: HC-05.pin5, Arduino_Pro_Mini_5V.D0/TX
  N14: HC-05.pin6, Arduino_Pro_Mini_5V.A0
  N15: IR1.Data, Arduino_Pro_Mini_5V.D2
  N16: MAGN_RESET.pin_1, Arduino_Pro_Mini_5V.RESET, Arduino_Pro_Mini_5V.D12/MISO
  N17: 10.pin2, Arduino_Pro_Mini_5V.D10_PWM/SS
  N18: proxim.pin1, proxim.pin2
  N19: proxy1.pin1, Arduino_Pro_Mini_5V.A1

notes:
  GND OUT 5v
  + -
  TSOP132x
  ST RX TX GND 5V KEY
  KEY 5V GND TX RX ST
  4CH relay ctrl.+1RGB pwm V1.0
  proxim
  proxy
  wired
  reed
  + G R B
  5v OUT GND
  GND
  VCC
  nc
